// Logisim project DIGITALCLOCK (1).circ as structural Verilog: 7 circuits, main circuit main
module main (
);

  wire and_1_out, and_2_out, and_3_out, and_4_out, and_5_out, and_6_out, and_7_out, and_8_out, and_9_out,
       and_10_out, and_11_out, clock_1_out, d_ff_1_qn, mod5counter_1_out_2, mod5counter_1_out_3,
       mod5counter_1_out_4, mod5counter_2_out_2, mod5counter_2_out_3, mod5counter_2_out_4,
       mod9_counter_1_out_4, mod9_counter_1_out_5, mod9_counter_1_out_6, mod9_counter_1_out_7,
       mod9_counter_2_out_4, mod9_counter_2_out_5, mod9_counter_2_out_6, mod9_counter_2_out_7,
       mod12counter_1_out_2, mod12counter_1_out_3, mod12counter_1_out_4, mod12counter_1_out_5,
       mod12counter_1_out_6, n0to5_7_segment_display_1_c_2, n0to5_7_segment_display_1_out_4,
       n0to5_7_segment_display_1_out_5, n0to5_7_segment_display_1_out_6, n0to5_7_segment_display_1_out_7,
       n0to5_7_segment_display_1_out_9, n0to5_7_segment_display_1_out_10, n0to5_7_segment_display_2_c_2,
       n0to5_7_segment_display_2_out_4, n0to5_7_segment_display_2_out_5, n0to5_7_segment_display_2_out_6,
       n0to5_7_segment_display_2_out_7, n0to5_7_segment_display_2_out_9, n0to5_7_segment_display_2_out_10,
       n7_segment_display_1_out_5, n7_segment_display_1_out_6, n7_segment_display_1_out_7,
       n7_segment_display_1_out_8, n7_segment_display_1_out_9, n7_segment_display_1_out_10,
       n7_segment_display_1_out_11, n7_segment_display_2_out_5, n7_segment_display_2_out_6,
       n7_segment_display_2_out_7, n7_segment_display_2_out_8, n7_segment_display_2_out_9,
       n7_segment_display_2_out_10, n7_segment_display_2_out_11, n7_segment_mod_12_1_out_5,
       n7_segment_mod_12_1_out_6, n7_segment_mod_12_1_out_7, n7_segment_mod_12_1_out_8,
       n7_segment_mod_12_1_out_9, n7_segment_mod_12_1_out_10, n7_segment_mod_12_1_out_11, nor_1_out,
       nor_2_out, not_1_out, not_2_out, not_3_out, not_4_out, not_5_out, not_6_out;

  and and_1 (and_1_out, nor_1_out, mod5counter_1_out_2);
  Clock clock_1 (.out(clock_1_out));
  and and_2 (and_2_out, and_1_out, and_3_out);
  and and_3 (and_3_out, not_1_out, not_2_out, not_3_out, mod9_counter_1_out_7);
  nor nor_1 (nor_1_out, mod5counter_1_out_3, mod5counter_1_out_4);
  and and_4 (and_4_out, mod5counter_1_out_2, mod5counter_1_out_3);
  and and_5 (and_5_out, nor_2_out, mod5counter_2_out_2);
  not not_1 (not_1_out, mod9_counter_1_out_4);
  not not_2 (not_2_out, mod9_counter_1_out_5);
  not not_3 (not_3_out, mod9_counter_1_out_6);
  and and_6 (and_6_out, and_5_out, and_7_out);
  and and_7 (and_7_out, not_4_out, not_5_out, not_6_out, mod9_counter_2_out_7);
  nor nor_2 (nor_2_out, mod5counter_2_out_3, mod5counter_2_out_4);
  and and_8 (and_8_out, mod5counter_2_out_2, mod5counter_2_out_3);
  MOD9_COUNTER mod9_counter_1 (
    .in_1(clock_1_out), .in_2(and_2_out), .in_3(and_2_out), .out_4(mod9_counter_1_out_4),
    .out_5(mod9_counter_1_out_5), .out_6(mod9_counter_1_out_6), .out_7(mod9_counter_1_out_7));
  MOD5COUNTER mod5counter_1 (
    .in_1(and_9_out), .out_2(mod5counter_1_out_2), .out_3(mod5counter_1_out_3), .out_4(mod5counter_1_out_4));
  not not_4 (not_4_out, mod9_counter_2_out_4);
  not not_5 (not_5_out, mod9_counter_2_out_5);
  not not_6 (not_6_out, mod9_counter_2_out_6);
  MOD9_COUNTER mod9_counter_2 (
    .in_1(and_4_out), .in_2(and_6_out), .in_3(and_6_out), .out_4(mod9_counter_2_out_4),
    .out_5(mod9_counter_2_out_5), .out_6(mod9_counter_2_out_6), .out_7(mod9_counter_2_out_7));
  MOD5COUNTER mod5counter_2 (
    .in_1(and_11_out), .out_2(mod5counter_2_out_2), .out_3(mod5counter_2_out_3), .out_4(mod5counter_2_out_4));
  Mod12Counter mod12counter_1 (
    .in_1(and_8_out), .out_2(mod12counter_1_out_2), .out_3(mod12counter_1_out_3),
    .out_4(mod12counter_1_out_4), .out_5(mod12counter_1_out_5), .out_6(mod12counter_1_out_6));
  _7_SEGMENT_DISPLAY u_7_segment_display_1 (
    .a(mod9_counter_1_out_7), .b(mod9_counter_1_out_6), .c(mod9_counter_1_out_5), .d(mod9_counter_1_out_4),
    .out_5(n7_segment_display_1_out_5), .out_6(n7_segment_display_1_out_6),
    .out_7(n7_segment_display_1_out_7), .out_8(n7_segment_display_1_out_8),
    .out_9(n7_segment_display_1_out_9), .out_10(n7_segment_display_1_out_10),
    .out_11(n7_segment_display_1_out_11));
  and and_9 (and_9_out, mod9_counter_1_out_5, mod9_counter_1_out_7);
  _0to5_7_segment_display u_0to5_7_segment_display_1 (
    .B(mod5counter_1_out_3), .c(mod5counter_1_out_2), .D(mod5counter_1_out_4),
    .out_4(n0to5_7_segment_display_1_out_4), .out_5(n0to5_7_segment_display_1_out_5),
    .out_6(n0to5_7_segment_display_1_out_6), .out_7(n0to5_7_segment_display_1_out_7),
    .C_2(n0to5_7_segment_display_1_c_2), .out_9(n0to5_7_segment_display_1_out_9),
    .out_10(n0to5_7_segment_display_1_out_10));
  and and_10 (and_10_out, mod12counter_1_out_3, mod12counter_1_out_5);
  _7_SEGMENT_DISPLAY u_7_segment_display_2 (
    .a(mod9_counter_2_out_7), .b(mod9_counter_2_out_6), .c(mod9_counter_2_out_5), .d(mod9_counter_2_out_4),
    .out_5(n7_segment_display_2_out_5), .out_6(n7_segment_display_2_out_6),
    .out_7(n7_segment_display_2_out_7), .out_8(n7_segment_display_2_out_8),
    .out_9(n7_segment_display_2_out_9), .out_10(n7_segment_display_2_out_10),
    .out_11(n7_segment_display_2_out_11));
  and and_11 (and_11_out, mod9_counter_2_out_5, mod9_counter_2_out_7);
  _0to5_7_segment_display u_0to5_7_segment_display_2 (
    .B(mod5counter_2_out_3), .c(mod5counter_2_out_2), .D(mod5counter_2_out_4),
    .out_4(n0to5_7_segment_display_2_out_4), .out_5(n0to5_7_segment_display_2_out_5),
    .out_6(n0to5_7_segment_display_2_out_6), .out_7(n0to5_7_segment_display_2_out_7),
    .C_2(n0to5_7_segment_display_2_c_2), .out_9(n0to5_7_segment_display_2_out_9),
    .out_10(n0to5_7_segment_display_2_out_10));
  _7_segment_mod_12 u_7_segment_mod_12_1 (
    .a(mod12counter_1_out_2), .b(mod12counter_1_out_3), .c(mod12counter_1_out_4), .d(mod12counter_1_out_5),
    .out_5(n7_segment_mod_12_1_out_5), .out_6(n7_segment_mod_12_1_out_6), .out_7(n7_segment_mod_12_1_out_7),
    .out_8(n7_segment_mod_12_1_out_8), .out_9(n7_segment_mod_12_1_out_9),
    .out_10(n7_segment_mod_12_1_out_10), .out_11(n7_segment_mod_12_1_out_11));
  D_Flip_Flop d_ff_1 (
    .clk(and_10_out), .D(d_ff_1_qn), .Qn(d_ff_1_qn), .reset(mod12counter_1_out_6));  // open: Q, preset, en
  _7_Segment_Display u_7_segment_display_3 (
    .g(n0to5_7_segment_display_1_out_7), .f(n0to5_7_segment_display_1_out_6),
    .a(n0to5_7_segment_display_1_out_4), .b(n0to5_7_segment_display_1_out_5),
    .e(n0to5_7_segment_display_1_out_10), .d(n0to5_7_segment_display_1_out_9),
    .c(n0to5_7_segment_display_1_c_2));  // open: dp
  _7_Segment_Display u_7_segment_display_4 (
    .g(n0to5_7_segment_display_2_out_7), .f(n0to5_7_segment_display_2_out_6),
    .a(n0to5_7_segment_display_2_out_4), .b(n0to5_7_segment_display_2_out_5),
    .e(n0to5_7_segment_display_2_out_10), .d(n0to5_7_segment_display_2_out_9),
    .c(n0to5_7_segment_display_2_c_2));  // open: dp
  _7_Segment_Display u_7_segment_display_5 (
    .f(d_ff_1_qn), .a(d_ff_1_qn), .b(1'b1), .e(d_ff_1_qn), .d(d_ff_1_qn), .c(1'b1));  // open: g, dp
  _7_Segment_Display u_7_segment_display_6 (
    .g(n7_segment_display_1_out_6), .f(n7_segment_display_1_out_11), .a(n7_segment_display_1_out_8),
    .b(n7_segment_display_1_out_9), .e(n7_segment_display_1_out_5), .d(n7_segment_display_1_out_7),
    .c(n7_segment_display_1_out_10));  // open: dp
  _7_Segment_Display u_7_segment_display_7 (
    .g(n7_segment_display_2_out_6), .f(n7_segment_display_2_out_11), .a(n7_segment_display_2_out_8),
    .b(n7_segment_display_2_out_9), .e(n7_segment_display_2_out_5), .d(n7_segment_display_2_out_7),
    .c(n7_segment_display_2_out_10));  // open: dp
  _7_Segment_Display u_7_segment_display_8 (
    .g(n7_segment_mod_12_1_out_11), .f(n7_segment_mod_12_1_out_10), .a(n7_segment_mod_12_1_out_5),
    .b(n7_segment_mod_12_1_out_6), .e(n7_segment_mod_12_1_out_9), .d(n7_segment_mod_12_1_out_8),
    .c(n7_segment_mod_12_1_out_7));  // open: dp

  // Notes on the sheet:
  //   2107088
  //   2107087
endmodule

module _7_SEGMENT_DISPLAY (
  input  a,
  input  b,
  input  c,
  input  d,
  output out_5,
  output out_6,
  output out_7,
  output out_8,
  output out_9,
  output out_10,
  output out_11
);

  wire and_1_out, b_prime_c_out, b_prime_d_prime_2_out, b_prime_d_prime_out, bc_prime_2_out, bc_prime_out,
       bd_out, bd_prime_2_out, bd_prime_out, c_prime_d_prime_prime_out, cd_out, cd_prime_out, not_1_out,
       not_2_out, not_3_out, not_4_out, not_5_out, not_6_out, not_7_out, not_8_out, not_9_out, not_10_out,
       not_11_out, not_12_out, not_13_out;

  not not_1 (not_1_out, b);
  not not_2 (not_2_out, b);
  not not_3 (not_3_out, c);
  not not_4 (not_4_out, d);
  not not_5 (not_5_out, b);
  not not_6 (not_6_out, not_4_out);
  not not_7 (not_7_out, not_6_out);
  not not_8 (not_8_out, not_2_out);
  not not_9 (not_9_out, c);
  not not_10 (not_10_out, not_6_out);
  and cd_prime (cd_prime_out, not_4_out, c);
  and b_prime_d_prime (b_prime_d_prime_out, not_5_out, not_4_out);
  and bd_prime (bd_prime_out, b, not_4_out);
  and bc_prime (bc_prime_out, b, not_3_out);
  and b_prime_c (b_prime_c_out, not_1_out, c);
  not not_11 (not_11_out, not_4_out);
  not not_12 (not_12_out, not_2_out);
  and bc_prime_2 (bc_prime_2_out, not_8_out, not_9_out);
  and bd_prime_2 (bd_prime_2_out, not_8_out, not_10_out);
  and and_1 (and_1_out, b, not_3_out, not_11_out);
  and bd (bd_out, b, not_6_out);
  and b_prime_d_prime_2 (b_prime_d_prime_2_out, not_2_out, not_7_out);
  xnor cd (cd_out, c, not_6_out);
  not not_13 (not_13_out, c);
  and c_prime_d_prime_prime (c_prime_d_prime_prime_out, not_9_out, not_10_out);
  or E (out_5, cd_prime_out, b_prime_d_prime_out);
  or G (out_6, bd_prime_out, bc_prime_out, b_prime_c_out, a);
  or u_D (out_7, cd_prime_out, b_prime_d_prime_out, b_prime_c_out, a, and_1_out);
  or u_A (out_8, bd_out, b_prime_d_prime_2_out, c, a);
  or u_B (out_9, cd_out, not_2_out);
  or u_C (out_10, not_13_out, not_12_out, not_6_out);
  or F (out_11, c_prime_d_prime_prime_out, bc_prime_2_out, bd_prime_2_out, a);

  // Notes on the sheet:
  //   2107088
endmodule

module _0to5_7_segment_display (
  input  B,
  input  c,
  input  D,
  output out_4,
  output out_5,
  output out_6,
  output out_7,
  output C_2,
  output out_9,
  output out_10
);

  wire and_1_out, B_prime_C_out, B_prime_D_prime_out, BC_prime_D_out, BD_out, C_prime_D_prime_2_out,
       C_prime_D_prime_out, CD_out, CD_prime_out, not_1_out, not_2_out, not_3_out;

  not not_1 (not_1_out, B);
  not not_2 (not_2_out, c);
  not not_3 (not_3_out, D);
  and BC_prime_D (BC_prime_D_out, B, not_2_out, D);
  and and_1 (and_1_out, B, not_2_out);
  and BD (BD_out, B, D);
  and B_prime_D_prime (B_prime_D_prime_out, not_1_out, not_3_out);
  and CD (CD_out, c, D);
  and C_prime_D_prime (C_prime_D_prime_out, not_2_out, not_3_out);
  and C_prime_D_prime_2 (C_prime_D_prime_2_out, B, not_3_out);
  and CD_prime (CD_prime_out, c, not_3_out);
  and B_prime_C (B_prime_C_out, not_1_out, c);
  or A (out_4, BD_out, B_prime_D_prime_out, c);
  or u_B (out_5, CD_out, C_prime_D_prime_out, not_1_out);
  or G (out_7, and_1_out, CD_prime_out, B_prime_C_out);
  or or_1 (C_2, B, not_2_out, D);
  or u_D (out_9, B_prime_D_prime_out, BC_prime_D_out, CD_prime_out, B_prime_C_out);
  or E (out_10, B_prime_D_prime_out, CD_prime_out);
  or F (out_6, C_prime_D_prime_out, C_prime_D_prime_2_out, and_1_out);

  // Notes on the sheet:
  //   2107088
endmodule

module MOD9_COUNTER (
  input  in_1,
  input  in_2,
  input  in_3,
  output out_4,
  output out_5,
  output out_6,
  output out_7
);

  wire and_1_out, d_ff_1_qn, d_ff_2_qn, d_ff_3_qn, d_ff_4_qn;

  D_Flip_Flop d_ff_1 (
    .clk(in_1), .D(d_ff_1_qn), .Q(out_4), .Qn(d_ff_1_qn), .preset(in_3), .reset(and_1_out));  // open: en
  D_Flip_Flop d_ff_2 (
    .clk(d_ff_1_qn), .D(d_ff_2_qn), .Q(out_5), .Qn(d_ff_2_qn), .reset(and_1_out));  // open: preset, en
  D_Flip_Flop d_ff_3 (
    .clk(d_ff_2_qn), .D(d_ff_3_qn), .Q(out_6), .Qn(d_ff_3_qn), .reset(and_1_out));  // open: preset, en
  D_Flip_Flop d_ff_4 (
    .clk(d_ff_3_qn), .D(d_ff_4_qn), .Q(out_7), .Qn(d_ff_4_qn), .preset(in_2), .reset(and_1_out));  // open: en
  and and_1 (and_1_out, out_5, out_7);

  // Notes on the sheet:
  //   2107088
endmodule

module MOD5COUNTER (
  input  in_1,
  output out_2,
  output out_3,
  output out_4
);

  wire and_1_out, d_ff_1_qn, d_ff_2_qn, d_ff_3_qn;

  D_Flip_Flop d_ff_1 (.clk(in_1), .D(d_ff_1_qn), .Q(out_4), .Qn(d_ff_1_qn), .reset(and_1_out));  // open: preset, en
  D_Flip_Flop d_ff_2 (
    .clk(d_ff_1_qn), .D(d_ff_2_qn), .Q(out_2), .Qn(d_ff_2_qn), .reset(and_1_out));  // open: preset, en
  D_Flip_Flop d_ff_3 (
    .clk(d_ff_2_qn), .D(d_ff_3_qn), .Q(out_3), .Qn(d_ff_3_qn), .reset(and_1_out));  // open: preset, en
  and and_1 (and_1_out, out_2, out_3);

  // Notes on the sheet:
  //   2107088
endmodule

module Mod12Counter (
  input  in_1,
  output out_2,
  output out_3,
  output out_4,
  output out_5,
  output out_6
);

  wire d_ff_1_qn, d_ff_2_qn, d_ff_3_qn, d_ff_4_qn;

  D_Flip_Flop d_ff_1 (.clk(in_1), .D(d_ff_1_qn), .Q(out_2), .Qn(d_ff_1_qn), .reset(out_6));  // open: preset, en
  D_Flip_Flop d_ff_2 (.clk(d_ff_1_qn), .D(d_ff_2_qn), .Q(out_3), .Qn(d_ff_2_qn), .reset(out_6));  // open: preset, en
  D_Flip_Flop d_ff_3 (.clk(d_ff_2_qn), .D(d_ff_3_qn), .Q(out_4), .Qn(d_ff_3_qn), .reset(out_6));  // open: preset, en
  D_Flip_Flop d_ff_4 (.clk(d_ff_3_qn), .D(d_ff_4_qn), .Q(out_5), .Qn(d_ff_4_qn), .reset(out_6));  // open: preset, en
  and and_1 (out_6, out_4, out_5);

  // Notes on the sheet:
  //   2107087
endmodule

module _7_segment_mod_12 (
  input  a,
  input  b,
  input  c,
  input  d,
  output out_5,
  output out_6,
  output out_7,
  output out_8,
  output out_9,
  output out_10,
  output out_11
);

  wire A_prime_B_prime_C_out, A_prime_C_out, AC_prime_2_out, AC_prime_out, AD_prime_out,
       B_prime_D_prime_2_out, B_prime_D_prime_out, BC_prime_2_out, BC_prime_D_out, BC_prime_out, BD_out,
       BD_prime_2_out, BD_prime_out, C_prime_D_prime_2_out, C_prime_D_prime_out, CD_out, CD_prime_out,
       not_1_out, not_2_out, not_3_out, not_4_out;

  not not_1 (not_1_out, a);
  not not_2 (not_2_out, b);
  not not_3 (not_3_out, c);
  not not_4 (not_4_out, d);
  and AC_prime (AC_prime_out, d, not_2_out);
  and A_prime_C (A_prime_C_out, not_4_out, b);
  and BD (BD_out, c, a);
  or u_A (out_5, A_prime_C_out, AC_prime_out, AC_prime_out, BD_out, B_prime_D_prime_out);
  and B_prime_D_prime (B_prime_D_prime_out, not_3_out, not_1_out);
  and CD (CD_out, b, a);
  or u_B (out_6, CD_out, C_prime_D_prime_out, not_3_out);
  and C_prime_D_prime (C_prime_D_prime_out, not_2_out, not_1_out);
  and AD_prime (AD_prime_out, d, not_1_out);
  or F (out_10, AD_prime_out, C_prime_D_prime_2_out, BD_prime_out, BC_prime_2_out, AC_prime_2_out);
  and BD_prime (BD_prime_out, c, not_1_out);
  and C_prime_D_prime_2 (C_prime_D_prime_2_out, not_2_out, not_1_out);
  and BC_prime (BC_prime_out, c, not_2_out);
  or G (out_11, BC_prime_out, BD_prime_2_out, AC_prime_2_out, A_prime_B_prime_C_out);
  and BD_prime_2 (BD_prime_2_out, c, not_1_out);
  or u_C (out_7, d, c, not_2_out, a);
  and CD_prime (CD_prime_out, b, not_1_out);
  and AC_prime_2 (AC_prime_2_out, d, not_2_out);
  or u_D (out_8, AC_prime_2_out, CD_prime_out, A_prime_B_prime_C_out, B_prime_D_prime_2_out, BC_prime_D_out);
  and B_prime_D_prime_2 (B_prime_D_prime_2_out, not_3_out, not_1_out);
  and A_prime_B_prime_C (A_prime_B_prime_C_out, not_4_out, not_3_out, b);
  or E (out_9, CD_prime_out, B_prime_D_prime_2_out);
  and BC_prime_D (BC_prime_D_out, a, BC_prime_2_out);
  and BC_prime_2 (BC_prime_2_out, c, not_2_out);

  // Notes on the sheet:
  //   2107087
endmodule
